# Fritzing sketch schema (saved by Fritzing 0.9.2b)
breadboards: 1

parts:
  Onderdeel1 = Arduino Uno (Rev3)
  U1 = ESP8266 WiFi Module [part_number=ESP8266]

nets:
  GND: Onderdeel1.GND, U1.GND
  N1: Onderdeel1.D0/RX, U1.RXD
  N2: Onderdeel1.D1/TX, U1.TXD
  3V3: Onderdeel1.3V3, U1.VCC, U1.CH_PD

custom parts:
  ESP8266 WiFi Module: Generic WiFi Module based on the ESP8266 with onboard PCB antenna and UART communications
